# Fritzing sketch Spark Core and Compressed Air Rocket Launcher (saved by Fritzing 0.9.0b)

parts:
  Spark_Core = Spark Core (v1.0)
  Relay_on_Shield = RELAY [package=relay-jzc]
  Push_Button = SWITCH-MOMENTARY-2 [package=tactile_switch_tall]
  Sprinkler_Valve_Solenoid = Solenoid
  Battery_in_Push_Button_Tube = Battery block 9V
  Battery_for_Relay_Shield = Battery block 9V

nets:
  N1: Spark_Core.GND, Relay_on_Shield.COIL1, Battery_for_Relay_Shield.-
  N2: Spark_Core.VIN, Battery_for_Relay_Shield.+
  N3: Spark_Core.D0, Relay_on_Shield.COIL2
  N4: Relay_on_Shield.NO, Push_Button.1, Sprinkler_Valve_Solenoid.pin2
  N5: Relay_on_Shield.MAIN, Push_Button.2, Battery_in_Push_Button_Tube.-
  N6: Sprinkler_Valve_Solenoid.pin1, Battery_in_Push_Button_Tube.+

notes:
  This isn't exact, but should give you the idea
